// Logisim project register.circ as structural Verilog: 1 circuit, main circuit main
module main (
);

  Decoder #(.select(5), .disabled(0)) decoder_1 ();  // open: out0, out1, out2, out3, out4, out5, out6, out7, out8, out9, out10, out11, out12, out13, out14, out15, out16, out17, out18, out19, out20, out21, out22, out23, out24, out25, out26, out27, out28, out29, out30, out31, sel, en
  Register #(.width(32)) register_1 ();  // open: D, en, Q, clk, clr
endmodule
